# Fritzing sketch Microview_DS1302 (saved by Fritzing 0.9.0b)
breadboards: 1

parts:
  MV1 = MicroView [part_number=MicroView package="16pin wide"]
  LED1 = RGB LED - (4 legs) [package="5 mm [THT]"]
  R1 = Resistor [tolerance=±5% resistance=470 package=THT]
  R2 = Resistor [tolerance=±5% resistance=470 package=THT]
  R3 = Resistor [tolerance=±5% resistance=470 package=THT]
  IC1 = DS1302 [package="DIP8 [THT]"]
  Y1 = CRYSTAL [package=crystal-32khz-smd]
  BAT2 = Battery Holders [package=battcon_12mm]

nets:
  N1: MV1.A2, IC1.CE_-_Chip_Enable
  N2: MV1.A1, IC1.SCLK_-_SPI_Clock
  N3: MV1.A0, IC1.I/O_-_SPI_Data_In/Out
  N4: MV1.GND, IC1.0V, BAT2.-
  N5: MV1.D3, R3.Pin_0
  N6: MV1.D5, R2.Pin_0
  N7: MV1.D6, R1.Pin_0
  N8: MV1.5V, LED1.common_anode, IC1.+V
  N9: LED1.red_cathode, R1.Pin_1
  N10: LED1.green_cathode, R2.Pin_1
  N11: LED1.blue_cathode, R3.Pin_1
  N12: IC1.X1_-_Crystal, Y1.2
  N13: IC1.X2_-_Crystal, Y1.1
  N14: IC1.Vbat_-_Backup_Supply, BAT2.+

custom parts:
  MicroView: MicroView - Chip-sized Arduino with OLED display.
